# Fritzing sketch receiver (saved by Fritzing 0.9.3b)
circuit board: 6.37607cm x 4.26564cm
breadboards: 1

parts:
  Q2 = Basic FET N-Channel [package="DPak [SMD]"]
  Q3 = Basic FET N-Channel [package="DPak [SMD]"]
  Q4 = Basic FET N-Channel [package="DPak [SMD]"]
  U3 = RJ45 Jack [package=rj45-8]
  LED1 = RGB LED (com. anode, rbg) [package="5 mm [THT]"]
  U4 = RJ45 Jack [package=rj45-8]
  Power_plug1 = Power plug
  R1 = Resistor [tolerance=±5% resistance=1k package=THT]
  R2 = Resistor [tolerance=±5% resistance=1k package=THT]
  R3 = Resistor [tolerance=±5% resistance=1k package=THT]
  R4 = Resistor [tolerance=±5% resistance=1k package=THT]
  R5 = Resistor [tolerance=±5% resistance=1k package=THT]
  R6 = Resistor [tolerance=±5% resistance=1k package=THT]

nets:
  N1: Q2.Gate, R3.Pin_0
  N2: Q2.drain, LED1.red_cathode
  N3: Q2.source, Q3.source, Q4.source, Power_plug1.GND
  N4: Q3.Gate, R2.Pin_0
  N5: Q3.drain, LED1.green_cathode
  N6: Q4.Gate, R1.Pin_0
  N7: Q4.drain, LED1.blue_cathode
  N8: U3.1, U3.2, U4.1, U4.2, R3.Pin_1, R6.Pin_0
  N9: U3.3, U3.4, U4.3, U4.4, R2.Pin_1, R5.Pin_0
  N10: U3.6, U4.5, U4.6
  N11: U3.7, U3.8, U4.7, U4.8, R1.Pin_1, R4.Pin_0
  N12: LED1.common_anode, Power_plug1.VCC, R4.Pin_1, R5.Pin_1, R6.Pin_1
